# Fritzing sketch Fritzing_Sketch2 (saved by Fritzing 0.9.4)

parts:
  Pro_Micro1 = SparkFun Pro Micro
  ENCODER1 = Rotary Encoder
  S1 = Round Pushbutton
  ENCODER2 = Rotary Encoder
  ENCODER3 = Rotary Encoder
  ENCODER4 = Rotary Encoder
  S2 = Round Pushbutton
  S3 = Square Pushbutton
  S4 = Round Pushbutton
  R1 = Resistor [tolerance=±5% resistance=220 package="2512 [SMD]"]
  LED1 = LED - 5mm [color="Red (633nm)" package="5 mm [THT]"]

nets:
  N1: Pro_Micro1.TX0, ENCODER3.CLK
  N2: Pro_Micro1.RX1, ENCODER3.GT
  N3: Pro_Micro1.GND, LED1.cathode
  N4: Pro_Micro1.2, ENCODER2.CLK
  N5: Pro_Micro1.3, ENCODER2.GT
  N6: Pro_Micro1.5, ENCODER4.CLK
  N7: Pro_Micro1.6, ENCODER1.CLK
  N8: Pro_Micro1.7, ENCODER1.GT
  N9: Pro_Micro1.8, ENCODER3.SW
  N10: Pro_Micro1.9, ENCODER2.SW
  N11: Pro_Micro1.10, S3.leg0
  N12: Pro_Micro1.16, ENCODER4.SW
  N13: Pro_Micro1.14, ENCODER1.SW
  N14: Pro_Micro1.15, S4.leg0
  N15: Pro_Micro1.A0, S2.leg0
  N16: Pro_Micro1.A1, S1.leg0
  N17: Pro_Micro1.A2, Pro_Micro1.A3, R1.Pin_0
  N18: R1.Pin_1, LED1.anode

custom parts:
  SparkFun Pro Micro: The Pro Micro is similar to the Pro Mini except with an ATmega32U4 on board. The USB transceiver inside the 32U4 allows us to add USB connectivity on-board and do away with bulky external USB interface. Based on: https://github.com/unorthodox-engineers/unorthodox-arduino/blob/master/Unorthodox/fritzing/parts/Pro%20Micro.fzpz
